# Fritzing sketch Hub (saved by Fritzing 0.9.3b)
circuit board: 6.48281cm x 12.0201cm
breadboards: 1

parts:
  1_5K = Resistor [tolerance=±5% resistance=220 package=THT]
  750 = Resistor [tolerance=±5% resistance=390 package=THT]
  82 = Resistor [tolerance=±5% resistance=75 package=THT]
  750_2 = Resistor [tolerance=±5% resistance=75 package=THT]
  Fan = LEDs [package=led-1206]
  LED = LEDs [package=led-1206]
  Heater = LEDs [package=led-1206]
  82_2 = Resistor [tolerance=±5% resistance=100 package=THT]
  OD_Regulator = Voltage Regulator [package=to220-igo]
  Sensor_Regulator = Voltage Regulator [package=to220-igo]
  Level_Regulator = Voltage Regulator [package=to220-igo]
  J545 = female pin header, 1 pin [form="♀ (female)"]  # not connected
  J546 = female pin header, 1 pin [form="♀ (female)"]
  J547 = female pin header, 1 pin [form="♀ (female)"]
  J548 = female pin header, 1 pin [form="♀ (female)"]
  J549 = female pin header, 1 pin [form="♀ (female)"]
  J550 = female pin header, 1 pin [form="♀ (female)"]
  J551 = female pin header, 1 pin [form="♀ (female)"]
  J552 = female pin header, 1 pin [form="♀ (female)"]
  J553 = female pin header, 1 pin [form="♀ (female)"]
  J554 = female pin header, 1 pin [form="♀ (female)"]  # not connected
  J555 = female pin header, 1 pin [form="♀ (female)"]  # not connected
  J556 = female pin header, 1 pin [form="♀ (female)"]
  J557 = female pin header, 1 pin [form="♀ (female)"]
  J558 = female pin header, 1 pin [form="♀ (female)"]
  J559 = female pin header, 1 pin [form="♀ (female)"]
  J560 = female pin header, 1 pin [form="♀ (female)"]
  J561 = female pin header, 1 pin [form="♀ (female)"]
  J562 = female pin header, 1 pin [form="♀ (female)"]  # not connected
  J563 = female pin header, 1 pin [form="♀ (female)"]  # not connected
  J564 = female pin header, 1 pin [form="♀ (female)"]  # not connected
  J565 = female pin header, 1 pin [form="♀ (female)"]  # not connected
  J566 = female pin header, 1 pin [form="♀ (female)"]
  J567 = female pin header, 1 pin [form="♀ (female)"]
  J568 = female pin header, 1 pin [form="♀ (female)"]
  J569 = female pin header, 1 pin [form="♀ (female)"]
  J5 = screw terminal, 14 pins
  J4 = screw terminal, 14 pins
  J571 = female pin header, 1 pin [form="♀ (female)"]
  J572 = female pin header, 1 pin [form="♀ (female)"]
  J573 = female pin header, 1 pin [form="♀ (female)"]

nets:
  N1: 1_5K.Pin_0, Heater.C
  GND: 1_5K.Pin_1, OD_Regulator.GND, Sensor_Regulator.GND, Level_Regulator.GND, J561.pin1, J5.pin11, J5.pin14, J4.pin9, J4.pin12, J571.pin1
  N2: 750.Pin_0, LED.A
  N3: 750.Pin_1, 82.Pin_0, OD_Regulator.OUT
  N4: 82.Pin_1, J4.pin5
  N5: 750_2.Pin_0, Fan.A
  N6: 750_2.Pin_1, Sensor_Regulator.IN, J566.pin1, J5.pin2, J5.pin4, J5.pin5, J4.pin4, J4.pin13
  N7: Fan.C, J546.pin1, J5.pin3
  N8: LED.C, J547.pin1, J4.pin6
  N9: Heater.A, J553.pin1, J5.pin8
  N10: 82_2.Pin_0, Level_Regulator.OUT
  N11: 82_2.Pin_1, J4.pin1
  N12: OD_Regulator.IN, Level_Regulator.IN, J558.pin1
  N13: Sensor_Regulator.OUT, J5.pin9, J5.pin12, J4.pin7, J4.pin10
  N14: J548.pin1, J4.pin2
  N15: J549.pin1, J572.pin1
  N16: J550.pin1, J5.pin1
  N17: J551.pin1, J4.pin14
  N18: J552.pin1, J5.pin7
  N19: J556.pin1, J4.pin8
  N20: J557.pin1, J5.pin13
  N21: J559.pin1, J4.pin11
  N22: J560.pin1, J5.pin10
  N23: J567.pin1, J573.pin1
  N24: J568.pin1, J5.pin6
  N25: J569.pin1, J4.pin3

notes:
  5V
  OD data
  GND
  level LED 5V
  level LED GND
  pump GND
  pump 12V
  OD LED 5V
  OD LED GND
  level LED data
  level data
  OD LED data
  heat 5V (Blk)
  fan GND
  heat GND (Red)
  fan 12V
  _____________
